# Fritzing sketch SprayingDevice (saved by Fritzing 0.8.7b)
breadboards: 1

parts:
  Part1 = Arduino Mega 2560 (Rev3)-TopMount
  SM2 = 28BYJ-48 Stepper Motor [part_number=28BYJ-48]
  U1 = prefix0000
  U2 = prefix0000
  U3 = prefix0000
  U4 = prefix0000
  Ultrasonic_Sensor1 = HC-SR04 [chip_label=IC package="SIP (Single Inline) [THT]"]
  Ultrasonic_Sensor2 = HC-SR04 [chip_label=IC package="SIP (Single Inline) [THT]"]
  Ultrasonic_Sensor3 = HC-SR04 [chip_label=IC package="SIP (Single Inline) [THT]"]
  SIM900 = sim800L v2 evb
  Relay_Module = Jtron 1 Channel Optoisolated Relay Module [package=relay]
  Up_Button = Round Pushbutton
  Set_Button = Round Pushbutton
  Bulk_Voltage = Mini-360 DC-DC Buck converter [package=THT]
  12V_Plug = Power plug
  12V_Plug1 = Power plug
  SM3 = 28BYJ-48 Stepper Motor [part_number=28BYJ-48]
  SM4 = 28BYJ-48 Stepper Motor [part_number=28BYJ-48]
  SM5 = 28BYJ-48 Stepper Motor [part_number=28BYJ-48]
  LCM1602_IIC1 = LCM1602 IIC [part_number="LCM1602 IIC" chip_label="LCM1602 IIC" package="DIP (Dual Inline) [THT]"]
  U5 = LCD-16X2 [package=lcd-16x2_noholes]
  Part2 = Voltage Sensor 25V
  12V_Battery = Battery block 9V
  12V_WATER_PUMP1 = water pump/motor
  Water_Level_Sensor1 = Water Level Sensor

nets:
  N1: Part1.A0, Part2.S
  N2: Part1.D21/SCL, LCM1602_IIC1.SCL
  N3: Part1.D20/SDA, LCM1602_IIC1.SDA
  N4: Part1.D19/RX1, SIM900.pin_4
  N5: Part1.D18/TX1, SIM900.pin_3
  N6: Part1.D13_PWM, U4.connector11
  N7: Part1.D12_PWM, U4.connector9
  N8: Part1.D11_PWM, U4.connector7
  N9: Part1.D10_PWM, U3.connector11
  N10: Part1.D9_PWM, U3.connector9
  N11: Part1.D8_PWM, U3.connector7
  5V: Part1.5V, Ultrasonic_Sensor1.Vcc, Ultrasonic_Sensor2.Vcc, Ultrasonic_Sensor3.Vcc, Relay_Module.VCC, LCM1602_IIC1.VCC, Part2.VCC, Part2.+, 12V_Battery.+, Water_Level_Sensor1.VCC
  GND: Part1.GND, U1.connector6, U1.connector8, U1.connector10, U2.connector6, U2.connector8, U2.connector10, U3.connector6, U3.connector8, U3.connector10, U4.connector6, U4.connector8, U4.connector10, Ultrasonic_Sensor1.GND, Ultrasonic_Sensor2.GND, Ultrasonic_Sensor3.GND, Relay_Module.GND, Up_Button.leg0, Set_Button.leg0, LCM1602_IIC1.GND, Part2.-, Water_Level_Sensor1.GND
  N12: Part1.D2_PWM, U1.connector7
  N13: Part1.D3_PWM, U1.connector9
  N14: Part1.D4_PWM, U1.connector11
  N15: Part1.D5_PWM, U2.connector7
  N16: Part1.D6_PWM, U2.connector9
  N17: Part1.D7_PWM, U2.connector11
  N18: Part1.D34, Water_Level_Sensor1.SIG
  N19: Part1.D36, Relay_Module.IN1
  N20: Part1.D38, Set_Button.leg1
  N21: Part1.D40, Up_Button.leg1
  N22: Part1.D42, Ultrasonic_Sensor3.Echo
  N23: Part1.D44, Ultrasonic_Sensor3.Trig
  N24: Part1.D46, Ultrasonic_Sensor2.Echo
  N25: Part1.D48, Ultrasonic_Sensor2.Trig
  N26: Part1.D50, Ultrasonic_Sensor1.Echo
  N27: Part1.D52, Ultrasonic_Sensor1.Trig
  N28: SM2.blue-pin, U1.connector0
  N29: SM2.yellow-pin, U1.connector2
  N30: SM2.orange-pin, U1.connector1
  N31: SM2.red-pin, U1.connector3
  N32: U1.connector4, U2.connector4, U3.connector4, U4.connector4, 12V_Plug1.VCC
  N33: U1.connector5, U2.connector5, U3.connector5, U4.connector5, 12V_Plug1.GND
  N34: U2.connector0, SM3.blue-pin
  N35: U2.connector1, SM3.orange-pin
  N36: U2.connector2, SM3.yellow-pin
  N37: U2.connector3, SM3.red-pin
  N38: U3.connector0, SM4.blue-pin
  N39: U3.connector1, SM4.orange-pin
  N40: U3.connector2, SM4.yellow-pin
  N41: U3.connector3, SM4.red-pin
  N42: U4.connector0, SM5.blue-pin
  N43: U4.connector1, SM5.orange-pin
  N44: U4.connector3, SM5.red-pin
  N45: SIM900.pin_2, SIM900.pin_6, Bulk_Voltage.OUT-
  N46: SIM900.pin_5, Bulk_Voltage.OUT+
  N47: Relay_Module.NC, 12V_WATER_PUMP1.pin_2
  N48: Relay_Module.MAIN, Bulk_Voltage.IN+, 12V_Plug.VCC
  N49: Bulk_Voltage.IN-, 12V_Plug.GND, 12V_WATER_PUMP1.pin_1
  VSS: LCM1602_IIC1.VSS, U5.VSS
  VDD: LCM1602_IIC1.VDD, U5.VDD
  N50: LCM1602_IIC1.V0, U5.VO
  N51: LCM1602_IIC1.RS, U5.RS
  N52: LCM1602_IIC1.RW, U5.R_W
  N53: LCM1602_IIC1.E, U5.E
  N54: LCM1602_IIC1.D0, U5.DB0
  N55: LCM1602_IIC1.D1, U5.DB1
  N56: LCM1602_IIC1.D2, U5.DB2
  N57: LCM1602_IIC1.D3, U5.DB3
  N58: LCM1602_IIC1.D4, U5.DB4
  N59: LCM1602_IIC1.D5, U5.DB5
  N60: LCM1602_IIC1.D6, U5.DB6
  N61: LCM1602_IIC1.D7, U5.DB7
  N62: LCM1602_IIC1.A, U5.A
  N63: LCM1602_IIC1.K, U5.K
  N64: Part2.GND, 12V_Battery.-

custom parts:
  Arduino Mega 2560 (Rev3)-TopMount: Arduino Mega 2560 (Rev3) for Top PCB Mount. The PCB view of the Arduino Mega 2560 (Rev3) in Arduino Bin flipped upside down with the text flipped back so as to be readable. Other views haven't changed Protruding component position is outlined to provide indication of part contact. Number in component outline is mm of protrusion of the component from the Mega PCB. Subtract the number from the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
  28BYJ-48 Stepper Motor: Unipolar Stepper Motor 28BYJ-48 Top coil - pink & orange Bottom coil - blue & yellow Common rail - red Connector pins: blue - pink - yellow - orange - red
  HC-SR04: HC-SR04 ultrasound distance sensor
  sim800L v2 evb: sim800L v2 evb GSM module.
  Mini-360 DC-DC Buck converter: Mini-360 DC-DC Buck converter. Tiny buck step down voltage converter, input voltage 4.75 to 23V output 1 to 17V adjustable. Available from ebay and the like.
  LCM1602 IIC: I2C-Module to use a 1602 or 2004 LCD on with the wire.h libory Serial LCD Modul
  water pump/motor: WATER PUMP BY ARDUBLOCKTR
  Water Level Sensor: A water level sensor. This sensor operates at 3V to 5V. The Sig (signal) pin outputs an analogue signal that is in proportion to the amount of water in contact with the sensor.
